# Fritzing sketch bike_motor_shim (saved by Fritzing 0.9.3b)
breadboards: 1

parts:
  Iskra1 = Iskra Mini
  D1 = Rectifier Diode [part_number=1N4001 package="300 mil [THT]"]
  R1 = Resistor [tolerance=±5% resistance=10k package=THT]
  J1 = female pin header, 4 pins [form="♀ (female)"]
  R2 = Resistor [tolerance=±5% resistance=220 package=THT]
  J2 = female pin header, 3 pins [form="♀ (female)"]
  R3 = Resistor [tolerance=±5% resistance=220 package=THT]

nets:
  GND: Iskra1.GND, D1.anode, R1.Pin_1, J1.pin3
  N1: Iskra1.D9_PWM, D1.cathode, R2.Pin_0
  N2: Iskra1.VCC, J2.pin1
  5V: Iskra1.5V, R3.Pin_1
  N3: Iskra1.D10_PWM, R1.Pin_0, J2.pin3
  N4: J1.pin2, R2.Pin_1
  N5: J2.pin2, R3.Pin_0

custom parts:
  Iskra Mini: The Arduino Mini is a small microcontroller board originally based on the ATmega168, but now supplied with the 328.(datasheet), intended for use on breadboards and when space is at a premium. It has 14 digital input/output pins (of which 6 can be used as PWM outputs), 8 analog inputs, and a 16 MHz crystal oscillator. It can be programmed with the USB Serial adapter or other USB or RS232 to TTL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
